// Digital circuit Final Diglo CPU (Format).dig as structural Verilog
module Final_Diglo_CPU__Format (
  input  reset,
  input  start,
  input  result,
  input  clk,
  input  progLoad,
  input  [7:0] M,
  input  [7:0] N,
  input  [12:0] progIN,
  output [7:0] accA,
  output [7:0] accB,
  output [7:0] regC,
  output [7:0] operand,
  output [4:0] opcode,
  output [7:0] \output ,
  output done,
  output [7:0] operand2,
  output valid,
  output [7:0] A,
  output [7:0] B,
  output [7:0] C,
  output [7:0] out_20
);

  wire _1, _2, _3, _4, _5, _6, _7, _8, _9, _10, _11, _12, _13, _14, _15, _16, _17, _18, _19, _20, _21, _22,
       _23, _24, _25, _26, _27, _28, _29, _30, _30store, _31, a_eq_b, a_eq_bs, a_eq_bstore, a_gt_b, a_lt_b,
       and_1_out, and_3_out, and_4_out, and_5_out, and_6_out, and_7_out, and_8_out, and_9_out, and_10_out,
       and_11_out, and_12_out, and_13_out, and_14_out, and_15_out, and_16_out, check, clk2, comparator_1_eq,
       comparator_1_gt, comparator_1_lt, comparator_3_eq, comparator_4_eq, done_t, equal, greater, jump,
       lesser, multiplexer_7_out, multiplexer_19_out, not_1_out, not_2_out, not_3_out, not_4_out, not_5_out,
       not_6_out, not_7_out, or_1_out, or_3_out, or_4_out, or_6_out, or_7_out, or_8_out, or_9_out, or_10_out,
       or_11_out, or_12_out, or_13_out, or_14_out, or_15_out, or_16_out, or_17_out, or_18_out, or_19_out,
       Prime_Rom_d, Qa, Qa_plus, Qb, Qb_plus, Qc, Qc_plus, S000, S001, S010, S011, S100, S101, valid_t;
  wire [2:0] bitcount_1_out;
  wire [4:0] demultiplexer_1_out_0, demultiplexer_1_out_1;
  wire [7:0] A_t, add, \and , B_t, count, counter_1_out, d_ff_4_q, d_ff_5_q, demultiplexer_4_out_0, div, gcd,
       m_t, mc, mod, mul, multiplexer_2_out, multiplexer_3_out, multiplexer_4_out, multiplexer_5_out,
       multiplexer_10_out, multiplexer_11_out, multiplexer_12_out, multiplexer_13_out, multiplexer_14_out,
       multiplexer_15_out, multiplexer_16_out, multiplexer_17_out, multiplexer_20_out, multiplexer_21_out,
       multiplexer_22_out, multiplexer_23_out, multiplexer_24_out, multiplexer_25_out, multiplexer_26_out,
       n_t, nc, not_8_out, operand3, \or , pow, re1, re2, Read_s, rRAM_d1, rRAM_d2, shift, sub, sub_2_s,
       Write__Read_out, \xor ;
  wire [11:0] count2;
  wire [12:0] multiplexer_8_out, pRAM_d1;
  wire [12:8] pRAM_d2;
  wire [15:0] mul_2_mul;

  and and_1 (and_1_out, ~start, ~reset, ~progLoad, ~result);  // And
  Add #(.Bits(8)) add_1 (.a(A), .b(accB), .c_i(1'b0), .s(add));  // open: c_o
  Sub #(.Bits(8)) sub_1 (.a(A), .b(accB), .c_i(1'b0), .s(sub));  // open: c_o
  Div #(.Bits(8)) div_1 (.a(A), .b(accB), .q(div), .r(mod));
  or or_1 (or_1_out, result, and_1_out);
  Mul #(.Bits(4)) mul_1 (.a(A[3:0]), .b(accB[3:0]), .mul(mul));
  BarrelShifter #(.Bits(8)) barrelshifter_1 (.in(A), .shift({1'b0, accB[2:0]}), .out(shift));
  Multiplexer #(.Selector_Bits(3)) multiplexer_1 (
    .sel({Qa, Qb, Qc}), .in_0(1'b0), .in_1(1'b0), .in_2(1'b0), .in_3(valid_t), .in_4(not_1_out),
    .in_5(not_2_out), .in_6(or_1_out), .in_7(1'b0), .out(Qa_plus));
  not not_1 (not_1_out, reset);
  not not_2 (not_2_out, reset);
  assign \and  = A & accB;  // And and_2, 8 bits wide
  assign \or  = A | accB;  // Or or_2, 8 bits wide
  assign \xor  = A ^ accB;  // XOr xor_1, 8 bits wide
  Add #(.Bits(8)) Read (.a(out_20), .b(8'h1), .c_i(1'b0), .s(Read_s));  // open: c_o
  D_FF d_ff_1 (.D(Qa_plus), .C(clk), .Q(Qa));  // open: nQ
  not not_3 (not_3_out, valid_t);
  ROM #(.AddrBits(6), .Bits(8)) Pow_Rom (.A({A[2:0], accB[2:0]}), .sel(1'b1), .D(pow));
  and and_3 (and_3_out, _13, equal);
  or or_3 (or_3_out, ~progLoad, start);  // Or
  and and_4 (and_4_out, not_3_out, ~reset);  // And
  Comparator #(.Signed("true"), .Bits(8)) comparator_1 (
    .a(A), .b(accB), .gt(comparator_1_gt), .eq(comparator_1_eq), .lt(comparator_1_lt));
  or or_4 (or_4_out, ~progLoad, reset);  // Or
  Multiplexer #(.Bits(8)) multiplexer_2 (.sel(jump), .in_0(Read_s), .in_1(operand), .out(multiplexer_2_out));
  or or_5 (jump, and_3_out, and_5_out, _12, and_8_out, and_10_out);
  and and_5 (and_5_out, _14, greater);
  and and_6 (and_6_out, not_4_out, ~reset);  // And
  not not_4 (not_4_out, progLoad);
  and and_7 (and_7_out, ~start, ~reset, ~progLoad, ~result);  // And
  ROM #(.AddrBits(8)) Prime_Rom (.A(A), .sel(1'b1), .D(Prime_Rom_d));
  Counter #(.Bits(8)) Write__Read (.en(progLoad), .C(clk), .clr(or_4_out), .out(Write__Read_out));  // open: ovf
  and and_8 (and_8_out, _15, lesser);
  and and_9 (and_9_out, ~reset, or_3_out);  // And
  or or_6 (or_6_out, start, and_7_out);
  Register register_1 (.D(comparator_1_gt), .C(clk), .en(_23), .Q(greater));
  Register register_2 (.D(comparator_1_lt), .C(clk), .en(_23), .Q(lesser));
  Multiplexer #(.Bits(8)) multiplexer_3 (.sel(S011), .in_0(Write__Read_out), .in_1(out_20), .out(multiplexer_3_out));
  or or_7 (or_7_out, start, S000);
  and and_10 (and_10_out, _16, or_8_out);
  or or_8 (or_8_out, equal, greater);
  D_FF d_ff_2 (.D(Qb_plus), .C(clk), .Q(Qb));  // open: nQ
  Multiplexer #(.Bits(8)) multiplexer_4 (.sel(_9), .in_0({8{1'b0}}), .in_1(operand), .out(multiplexer_4_out));
  Multiplexer #(.Bits(8)) multiplexer_5 (
    .sel(or_7_out), .in_0(multiplexer_2_out), .in_1({8{1'b0}}), .out(multiplexer_5_out));
  Multiplexer #(.Selector_Bits(3)) multiplexer_6 (
    .sel({Qa, Qb, Qc}), .in_0(start), .in_1(and_9_out), .in_2(and_6_out), .in_3(and_4_out), .in_4(1'b0),
    .in_5(done_t), .in_6(or_6_out), .in_7(1'b0), .out(Qb_plus));
  Multiplexer multiplexer_7 (.sel(_29), .in_0(comparator_1_eq), .in_1(Prime_Rom_d), .out(multiplexer_7_out));
  or or_9 (or_9_out, _23, _29);
  RAMDualAccess #(.AddrBits(8), .Bits(13)) pRAM (
    .str(progLoad), .C(clk), .ld(S011), .A1(multiplexer_3_out), .Din1(progIN), .A2(multiplexer_4_out),
    .D1(pRAM_d1), .D2({pRAM_d2, operand2}));
  or or_10 (or_10_out, S011, S000);
  D_FF d_ff_3 (.D(Qc_plus), .C(clk), .Q(Qc));  // open: nQ
  or or_11 (or_11_out, progLoad, start);
  Register register_3 (.D(multiplexer_7_out), .C(clk), .en(or_9_out), .Q(equal));
  Multiplexer #(.Bits(13)) multiplexer_8 (.sel(or_12_out), .in_0(pRAM_d1), .in_1({13{1'b0}}), .out(multiplexer_8_out));
  or or_12 (or_12_out, valid_t, jump);
  Register #(.Bits(8)) register_4 (.D(multiplexer_5_out), .C(clk), .en(or_10_out), .Q(out_20));
  not not_5 (not_5_out, valid_t);
  not not_6 (not_6_out, done_t);
  Register #(.Bits(13)) register_5 (.D(multiplexer_8_out), .C(clk), .en(S011), .Q({opcode, operand}));
  and and_11 (and_11_out, ~reset, or_11_out);  // And
  and and_12 (and_12_out, ~reset, not_5_out);  // And
  and and_13 (and_13_out, ~reset, not_6_out);  // And
  BitCount #(.Bits(5)) bitcount_1 (.in(opcode), .out(bitcount_1_out));
  or or_13 (or_13_out, progLoad, start);
  or or_14 (or_14_out, progLoad, start, result);
  Comparator #(.Bits(3)) comparator_2 (.a(bitcount_1_out), .b(3'b101), .eq(valid_t));  // open: gt, lt
  Counter #(.Bits(8)) counter_1 (.en(S000), .C(clk), .clr(S011), .out(counter_1_out));  // open: ovf
  Demultiplexer #(.Bits(5)) demultiplexer_1 (
    .sel(S100), .in(opcode), .out_0(demultiplexer_1_out_0), .out_1(demultiplexer_1_out_1));
  Multiplexer #(.Selector_Bits(3)) multiplexer_9 (
    .sel({Qa, Qb, Qc}), .in_0(or_13_out), .in_1(and_11_out), .in_2(start), .in_3(and_12_out), .in_4(result),
    .in_5(and_13_out), .in_6(or_14_out), .in_7(1'b0), .out(Qc_plus));
  Multiplexer #(.Bits(8)) multiplexer_10 (.sel(S000), .in_0(operand), .in_1(counter_1_out), .out(multiplexer_10_out));
  Multiplexer #(.Bits(8)) multiplexer_11 (.sel(S000), .in_0(A), .in_1({8{1'b0}}), .out(multiplexer_11_out));
  Comparator #(.Bits(8)) comparator_3 (.a(count), .b(8'he), .eq(comparator_3_eq));  // open: gt, lt
  Demultiplexer #(.Selector_Bits(5)) demultiplexer_2 (
    .sel(demultiplexer_1_out_0), .in(1'b1), .out_1(_1), .out_2(_2), .out_3(_3), .out_4(_4), .out_5(_5),
    .out_6(_6), .out_7(_7), .out_8(_8), .out_9(_9), .out_10(_10), .out_11(_11), .out_12(_12), .out_13(_13),
    .out_14(_14), .out_15(_15), .out_16(_16), .out_17(_17), .out_18(_18), .out_19(_19), .out_20(_20),
    .out_21(_21), .out_22(_22), .out_23(_23), .out_24(_24), .out_25(_25), .out_26(_26), .out_27(_27),
    .out_28(_28), .out_29(_29), .out_30(_30), .out_31(_31));  // open: out_0
  Decoder #(.Selector_Bits(3)) decoder_1 (
    .sel({Qa, Qb, Qc}), .out_0(S000), .out_1(S001), .out_2(S010), .out_3(S011), .out_4(S100), .out_5(S101),
    .out_6(done));  // open: out_7
  Multiplexer #(.Bits(8)) multiplexer_12 (
    .sel(_30), .in_0(multiplexer_10_out), .in_1({4'b0000, operand[7:4]}), .out(multiplexer_12_out));
  Multiplexer #(.Bits(8)) multiplexer_13 (
    .sel(a_eq_bs), .in_0(multiplexer_12_out), .in_1(8'he), .out(multiplexer_13_out));
  Multiplexer #(.Bits(8)) multiplexer_14 (
    .sel(a_eq_bs), .in_0(multiplexer_11_out), .in_1(re1), .out(multiplexer_14_out));
  Register register_6 (.D(comparator_3_eq), .C(clk), .en(S101), .Q(done_t));
  or or_15 (or_15_out, S000, _11, a_eq_bs, a_eq_bstore);
  or or_16 (or_16_out, _10, _30);
  Multiplexer #(.Bits(8)) multiplexer_15 (
    .sel(a_eq_bstore), .in_0(multiplexer_13_out), .in_1(8'hf), .out(multiplexer_15_out));
  Multiplexer #(.Bits(8)) multiplexer_16 (
    .sel(a_eq_bstore), .in_0(multiplexer_14_out), .in_1(re2), .out(multiplexer_16_out));
  RAMDualAccess #(.AddrBits(8), .Bits(8)) rRAM (
    .str(or_15_out), .C(clk), .ld(or_16_out), .A1(multiplexer_15_out), .Din1(multiplexer_16_out),
    .A2(multiplexer_17_out), .D1(rRAM_d1), .D2(rRAM_d2));
  Multiplexer #(.Bits(8)) multiplexer_17 (
    .sel(_30), .in_0(count), .in_1({4'b0000, operand[3:0]}), .out(multiplexer_17_out));
  Comparator #(.Bits(8)) comparator_4 (.a(count), .b(8'h10), .eq(comparator_4_eq));  // open: gt, lt
  Demultiplexer #(.Bits(8)) demultiplexer_3 (.sel(_30), .in(rRAM_d1), .out_0(operand3), .out_1(mc));
  Demultiplexer #(.Bits(8)) demultiplexer_4 (.sel(_30), .in(rRAM_d2), .out_0(demultiplexer_4_out_0), .out_1(nc));
  not not_7 (not_7_out, comparator_4_eq);
  assign not_8_out = ~A;  // Not not_8, 8 bits wide
  or or_17 (or_17_out, _1, _3, _6, _9, _10, _17, _18, _19, _20, _21, _22, _24, _25, _26, _27, _28);
  Multiplexer #(.Bits(8)) multiplexer_18 (.sel(S101), .in_0({8{1'b0}}), .in_1(demultiplexer_4_out_0), .out(\output ));
  Multiplexer multiplexer_19 (.sel(S101), .in_0(1'b0), .in_1(not_7_out), .out(multiplexer_19_out));
  Multiplexer #(.Selector_Bits(5), .Bits(8)) multiplexer_20 (
    .sel(opcode), .in_0({8{1'b0}}), .in_1(operand), .in_2({8{1'b0}}), .in_3(accB), .in_4({8{1'b0}}),
    .in_5({8{1'b0}}), .in_6(C), .in_7({8{1'b0}}), .in_8({8{1'b0}}), .in_9(operand2), .in_10(operand3),
    .in_11({8{1'b0}}), .in_12({8{1'b0}}), .in_13({8{1'b0}}), .in_14({8{1'b0}}), .in_15({8{1'b0}}),
    .in_16({8{1'b0}}), .in_17(add), .in_18(sub), .in_19(mul), .in_20(div), .in_21(mod), .in_22(pow),
    .in_23({8{1'b0}}), .in_24(not_8_out), .in_25(\and ), .in_26(\or ), .in_27(\xor ), .in_28(shift),
    .in_29({8{1'b0}}), .in_30({8{1'b0}}), .in_31({8{1'b0}}), .out(multiplexer_20_out));
  Counter #(.Bits(8)) counter_2 (.en(multiplexer_19_out), .C(clk), .clr(done), .out(count));  // open: ovf
  and and_14 (and_14_out, or_17_out, S011);
  or or_18 (or_18_out, _2, _4);
  and and_15 (and_15_out, or_18_out, S011);
  Seven_Seg_Hex seven_seg_hex_1 (.d(\output [7:4]), .dp(1'b0));
  Register #(.Bits(8)) u_accA (.D(multiplexer_20_out), .C(clk), .en(and_14_out), .Q(A));
  Multiplexer #(.Bits(8)) multiplexer_21 (.sel(_4), .in_0(operand), .in_1(A), .out(multiplexer_21_out));
  Register #(.Bits(8)) u_accB (.D(multiplexer_21_out), .C(clk), .en(and_15_out), .Q(accB));
  Seven_Seg_Hex seven_seg_hex_2 (.d(\output [3:0]), .dp(1'b0));
  or or_19 (or_19_out, _5, _7, _8);
  Multiplexer #(.Selector_Bits(5), .Bits(8)) multiplexer_22 (
    .sel(opcode), .in_0({8{1'b0}}), .in_1({8{1'b0}}), .in_2({8{1'b0}}), .in_3({8{1'b0}}), .in_4({8{1'b0}}),
    .in_5(A), .in_6({8{1'b0}}), .in_7(M), .in_8(N), .in_9({8{1'b0}}), .in_10({8{1'b0}}), .in_11({8{1'b0}}),
    .in_12({8{1'b0}}), .in_13({8{1'b0}}), .in_14({8{1'b0}}), .in_15({8{1'b0}}), .in_16({8{1'b0}}),
    .in_17({8{1'b0}}), .in_18({8{1'b0}}), .in_19({8{1'b0}}), .in_20({8{1'b0}}), .in_21({8{1'b0}}),
    .in_22({8{1'b0}}), .in_23({8{1'b0}}), .in_24({8{1'b0}}), .in_25({8{1'b0}}), .in_26({8{1'b0}}),
    .in_27({8{1'b0}}), .in_28({8{1'b0}}), .in_29({8{1'b0}}), .in_30({8{1'b0}}), .in_31({8{1'b0}}),
    .out(multiplexer_22_out));
  and and_16 (and_16_out, or_19_out, S011);
  Register #(.Bits(8)) u_regC (.D(multiplexer_22_out), .C(clk), .en(and_16_out), .Q(C));
  or or_20 (valid, S100, S101, done);
  Register #(.Bits(8)) register_7 (.D(mc), .C(clk), .en(_30), .Q(m_t));
  Register #(.Bits(8)) register_8 (.D(nc), .C(clk), .en(_30), .Q(n_t));
  Register register_9 (.D(_30), .C(clk), .en(_30), .Q(_30store));
  Register register_10 (.D(a_eq_bs), .C(clk), .en(a_eq_bs), .Q(a_eq_bstore));
  and and_17 (clk2, _30store, clk);
  Counter #(.Bits(12)) counter_3 (.en(clk2), .C(clk2), .clr(1'b0), .out(count2));  // open: ovf
  Comparator #(.Bits(12)) comparator_5 (.a(count2), .b({12{1'b0}}), .gt(check));  // open: eq, lt
  Multiplexer #(.Bits(8)) multiplexer_23 (.sel(check), .in_0(m_t), .in_1(A_t), .out(multiplexer_23_out));
  Multiplexer #(.Bits(8)) multiplexer_24 (.sel(check), .in_0(n_t), .in_1(B_t), .out(multiplexer_24_out));
  D_FF #(.Bits(8)) d_ff_4 (.D(multiplexer_23_out), .C(clk2), .Q(d_ff_4_q));  // open: nQ
  D_FF #(.Bits(8)) d_ff_5 (.D(multiplexer_24_out), .C(clk2), .Q(d_ff_5_q));  // open: nQ
  Mul #(.Bits(8)) mul_2 (.a(m_t), .b(n_t), .mul(mul_2_mul));
  Div #(.Bits(16)) div_2 (.a(mul_2_mul), .b({{8{1'b0}}, gcd}), .q({re1, re2}));  // open: r
  Multiplexer #(.Bits(8)) multiplexer_25 (.sel(a_gt_b), .in_0(d_ff_5_q), .in_1(d_ff_4_q), .out(multiplexer_25_out));
  Multiplexer #(.Bits(8)) multiplexer_26 (.sel(a_lt_b), .in_0(d_ff_5_q), .in_1(d_ff_4_q), .out(multiplexer_26_out));
  Comparator #(.Bits(8)) comparator_6 (.a(d_ff_4_q), .b(d_ff_5_q), .gt(a_gt_b), .eq(a_eq_b), .lt(a_lt_b));
  Sub #(.Bits(8)) sub_2 (.a(multiplexer_25_out), .b(multiplexer_26_out), .c_i(1'b0), .s(sub_2_s));  // open: c_o
  Multiplexer #(.Bits(8)) multiplexer_27 (.sel(a_eq_b), .in_0({8{1'b0}}), .in_1(d_ff_5_q), .out(gcd));
  and and_18 (a_eq_bs, a_eq_b, _30store);
  Multiplexer #(.Bits(8)) multiplexer_28 (.sel(a_gt_b), .in_0(d_ff_4_q), .in_1(sub_2_s), .out(A_t));
  Multiplexer #(.Bits(8)) multiplexer_29 (.sel(a_lt_b), .in_0(d_ff_5_q), .in_1(sub_2_s), .out(B_t));

  assign accA = A;
  assign B = accB;
  assign regC = C;
  // also tied to GND on the sheet: {demultiplexer_1_out_1[0], demultiplexer_1_out_1[1], demultiplexer_1_out_1[2], demultiplexer_1_out_1[3], demultiplexer_1_out_1[4]}

  // Other names for the same wires on the sheet: g1[3:0] = operand[3:0]; g2[3:0] = operand[7:4]; in[7:0] = out_20;
  //   S110 = done; str = start

  // Notes on the sheet:
  //   Input
  //   Control unit
  //   Operand
  //   pRAM
  //   contents of Pow_Rom (hex, n*v repeats v):
  //   1,7*0,9*1,2,4,8,10,20,40,80,1,3,9,1b,51,f3,2d9,88b,1,4,10,40,100
  //   ,400,0,0,1,5,19,7d,271,c35,3d09,2d,1,6,24,d8,510,1e60,b640,44580
  //   ,1,7,31,157,961,41a7,1cb91,c90f7
  //   contents of Prime_Rom (hex, n*v repeats v):
  //   0,0,1,1,0,1,0,1,0,0,0,1,0,1,0,0,0,1,0,1,0,0,0,1,5*0,1,0,1,5*0
  //   ,1,0,0,0,1,0,1,0,0,0,1,5*0,1,5*0,1,0,1,5*0,1,0,0,0,1,0,1,5*0,1
  //   ,0,0,0,1,5*0,1,7*0,1,0,0,0,1,0,1,0,0,0,1,0,1,0,0,0,1,13*0,1,0,0,0
  //   ,1,5*0,1,0,1,9*0,1,0,1,5*0,1,5*0,1,0,0,0,1,5*0,1,5*0,1,0,1,9*0
  //   ,1,0,1,0,0,0,1,0,1,11*0,1,11*0,1,0,0,0,1,0,1,0,0,0,1,5*0,1,0,1
  //   ,9*0,1
  //   rRAM & Output
  //   reset -> S000
  //   progload -> S001
  //   start -> S011
  //   valid -> S100
  //   result -> S101
  //   done -> S110
  //   Register
  //   1A use for write 11 write reset(0) and read 10
  //   2A use for show result
  //   Testcase
  //   Done
  //   Valid
  //   LCM
endmodule

/* Test case order play with reset:
M	N	progIN	reset	progLoad	start	result	clk	valid	done	output
0	0	0	0	0	0	0	0	x	x	x
0	0	0	0	0	0	0	1	x	x	x
0	0	0	1	0	0	0	0	0	0	0
0	0	0	1	0	0	0	1	0	0	0
0	0	0	0	0	0	0	0	0	0	0
0	0	0	0	0	0	0	1	0	0	0
0	0	0	0	0	0	0	0	0	0	0
0	0	0	0	0	0	0	1	0	0	0
0	0	0	0	0	0	0	0	0	0	0
0	0	0	0	0	0	0	1	0	0	0
0	0	0	0	0	0	0	0	0	0	0
0	0	0	0	0	0	0	1	0	0	0
0	0	0	0	0	0	0	0	0	0	0
0	0	0	0	0	0	0	1	0	0	0
0	0	0	0	0	0	0	0	0	0	0
0	0	0	0	0	0	0	1	0	0	0
0	0	0	0	0	0	0	0	0	0	0
0	0	0	0	0	0	0	1	0	0	0
0	0	0	0	0	0	0	0	0	0	0
0	0	0	0	0	0	0	1	0	0	0
0	0	0	0	0	0	0	0	0	0	0
0	0	0	0	0	0	0	1	0	0	0
0	0	0	0	0	0	0	0	0	0	0
0	0	0	0	0	0	0	1	0	0	0
0	0	0	0	0	0	0	0	0	0	0
0	0	0	0	0	0	0	1	0	0	0
0	0	0	0	0	0	0	0	0	0	0
0	0	0	0	0	0	0	1	0	0	0
0	0	0	0	0	0	0	0	0	0	0
0	0	0	0	0	0	0	1	0	0	0
0	0	0	0	0	0	0	0	0	0	0
0	0	0	0	0	0	0	1	0	0	0
0	0	0	0	0	0	0	0	0	0	0
0	0	0	0	0	0	0	1	0	0	0
0	0	0	0	0	0	0	0	0	0	0
0	0	0	0	0	0	0	1	0	0	0
0	0	0	0	0	0	0	0	0	0	0
0	0	0	0	0	0	0	1	0	0	0
0	0	0	0	0	0	0	0	0	0	0
0	0	0	0	0	0	0	1	0	0	0
0	0	0	0	0	0	0	0	0	0	0
0	0	0	0	0	0	0	1	0	0	0
0	0	257	0	1	0	0	0	0	0	0
0	0	257	0	1	0	0	1	0	0	0
0	0	2816	0	1	0	0	0	0	0	0
0	0	2816	0	1	0	0	1	0	0	0
0	0	266	0	1	0	0	0	0	0	0
0	0	266	0	1	0	0	1	0	0	0
0	0	2817	0	1	0	0	0	0	0	0
0	0	2817	0	1	0	0	1	0	0	0
0	0	356	0	1	0	0	0	0	0	0
0	0	356	0	1	0	0	1	0	0	0
0	0	2818	0	1	0	0	0	0	0	0
0	0	2818	0	1	0	0	1	0	0	0
0	0	383	0	1	0	0	0	0	0	0
0	0	383	0	1	0	0	1	0	0	0
0	0	2819	0	1	0	0	0	0	0	0
0	0	2819	0	1	0	0	1	0	0	0
0	0	7936	0	1	0	0	0	0	0	0
0	0	7936	0	1	0	0	1	0	0	0
0	0	0	0	0	1	0	0	0	0	0
0	0	0	0	0	1	0	1	0	0	0
0	0	0	0	0	0	0	0	x	0	0
0	0	0	0	0	0	0	1	x	0	0
0	0	0	0	0	0	0	0	x	0	0
0	0	0	0	0	0	0	1	x	0	0
0	0	0	0	0	0	0	0	x	0	0
0	0	0	0	0	0	0	1	x	0	0
0	0	0	0	0	0	0	0	x	0	0
0	0	0	0	0	0	0	1	x	0	0
0	0	0	0	0	0	0	0	x	0	0
0	0	0	0	0	0	0	1	x	0	0
0	0	0	0	0	0	0	0	x	0	0
0	0	0	0	0	0	0	1	x	0	0
0	0	0	0	0	0	0	0	x	0	0
0	0	0	0	0	0	0	1	x	0	0
0	0	0	0	0	0	0	0	x	0	0
0	0	0	0	0	0	0	1	x	0	0
0	0	0	0	0	0	0	0	x	0	0
0	0	0	0	0	0	0	1	x	0	0
0	0	0	0	0	0	0	0	x	0	0
0	0	0	0	0	0	0	1	x	0	0
0	0	0	0	0	0	0	0	x	0	0
0	0	0	0	0	0	0	1	x	0	0
0	0	0	0	0	0	0	0	x	0	0
0	0	0	0	0	0	0	1	x	0	0
0	0	0	0	0	0	0	0	x	0	0
0	0	0	0	0	0	0	1	x	0	0
0	0	0	0	0	0	0	0	x	0	0
0	0	0	0	0	0	0	1	x	0	0
0	0	0	0	0	0	0	0	x	0	0
0	0	0	0	0	0	0	1	x	0	0
0	0	0	0	0	0	0	0	x	0	0
0	0	0	0	0	0	0	1	x	0	0
0	0	0	0	0	0	0	0	x	0	0
0	0	0	0	0	0	0	1	x	0	0
0	0	0	0	0	0	0	0	x	0	0
0	0	0	0	0	0	0	1	x	0	0
0	0	0	0	0	0	0	0	x	0	0
0	0	0	0	0	0	0	1	x	0	0
0	0	0	0	0	0	0	0	x	0	0
0	0	0	0	0	0	0	1	x	0	0
0	0	0	0	0	0	0	0	x	0	0
0	0	0	0	0	0	0	1	x	0	0
0	0	0	0	0	0	0	0	x	0	0
0	0	0	0	0	0	0	1	x	0	0
0	0	0	0	0	0	0	0	x	0	0
0	0	0	0	0	0	0	1	x	0	0
0	0	0	0	0	0	0	0	x	0	0
0	0	0	0	0	0	0	1	x	0	0
0	0	0	0	0	0	0	0	x	0	0
0	0	0	0	0	0	0	1	x	0	0
0	0	0	0	0	0	0	0	x	0	0
0	0	0	0	0	0	0	1	1	0	0
0	0	0	1	0	0	0	0	1	0	0
0	0	0	1	0	0	0	1	0	0	0
0	0	0	0	0	0	0	0	0	0	0
0	0	0	0	0	0	0	1	0	0	0
0	0	0	0	0	0	0	0	0	0	0
0	0	0	0	0	0	0	1	0	0	0
0	0	0	0	0	0	0	0	0	0	0
0	0	0	0	0	0	0	1	0	0	0
0	0	0	0	0	0	0	0	0	0	0
0	0	0	0	0	0	0	1	0	0	0
0	0	0	0	0	0	0	0	0	0	0
0	0	0	0	0	0	0	1	0	0	0
0	0	0	0	0	0	0	0	0	0	0
0	0	0	0	0	0	0	1	0	0	0
0	0	0	0	0	0	0	0	0	0	0
0	0	0	0	0	0	0	1	0	0	0
0	0	0	0	0	0	0	0	0	0	0
0	0	0	0	0	0	0	1	0	0	0
0	0	0	0	0	0	0	0	0	0	0
0	0	0	0	0	0	0	1	0	0	0
0	0	0	0	0	0	0	0	0	0	0
0	0	0	0	0	0	0	1	0	0	0
0	0	0	0	0	0	0	0	0	0	0
0	0	0	0	0	0	0	1	0	0	0
0	0	0	0	0	0	0	0	0	0	0
0	0	0	0	0	0	0	1	0	0	0
0	0	0	0	0	0	0	0	0	0	0
0	0	0	0	0	0	0	1	0	0	0
0	0	0	0	0	0	0	0	0	0	0
0	0	0	0	0	0	0	1	0	0	0
0	0	0	0	0	0	0	0	0	0	0
0	0	0	0	0	0	0	1	0	0	0
0	0	0	0	0	0	0	0	0	0	0
0	0	0	0	0	0	0	1	0	0	0
0	0	0	0	0	0	0	0	0	0	0
0	0	0	0	0	0	0	1	0	0	0
0	0	0	0	0	0	0	0	0	0	0
0	0	0	0	0	0	0	1	0	0	0
0	0	0	0	0	0	0	0	0	0	0
0	0	0	0	0	0	0	1	0	0	0
0	0	271	0	1	0	0	0	0	0	0
0	0	271	0	1	0	0	1	0	0	0
0	0	559	0	1	0	0	0	0	0	0
0	0	559	0	1	0	0	1	0	0	0
0	0	4352	0	1	0	0	0	0	0	0
0	0	4352	0	1	0	0	1	0	0	0
0	0	2817	0	1	0	0	0	0	0	0
0	0	2817	0	1	0	0	1	0	0	0
0	0	7936	0	1	0	0	0	0	0	0
0	0	7936	0	1	0	0	1	0	0	0
0	0	2818	0	1	0	0	0	0	0	0
0	0	2818	0	1	0	0	1	0	0	0
0	0	0	0	0	1	0	0	0	0	0
0	0	0	0	0	1	0	1	0	0	0
0	0	0	0	0	0	0	0	x	0	0
0	0	0	0	0	0	0	1	x	0	0
0	0	0	0	0	0	0	0	x	0	0
0	0	0	0	0	0	0	1	x	0	0
0	0	0	0	0	0	0	0	x	0	0
0	0	0	0	0	0	0	1	x	0	0
0	0	0	0	0	0	0	0	x	0	0
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*/

/* Test case TF:
M	N	progIN	reset	progLoad	start	result	clk	valid	done	output
0	0	0	0	0	0	0	0	x	x	x
0	0	0	0	0	0	0	1	x	x	x
0	0	0	1	0	0	0	0	0	0	0
0	0	0	1	0	0	0	1	0	0	0
0	0	0	0	0	0	0	0	0	0	0
0	0	0	0	0	0	0	1	0	0	0
0	0	0	0	0	0	0	0	0	0	0
0	0	0	0	0	0	0	1	0	0	0
0	0	0	0	0	0	0	0	0	0	0
0	0	0	0	0	0	0	1	0	0	0
0	0	0	0	0	0	0	0	0	0	0
0	0	0	0	0	0	0	1	0	0	0
0	0	0	0	0	0	0	0	0	0	0
0	0	0	0	0	0	0	1	0	0	0
0	0	0	0	0	0	0	0	0	0	0
0	0	0	0	0	0	0	1	0	0	0
0	0	0	0	0	0	0	0	0	0	0
0	0	0	0	0	0	0	1	0	0	0
0	0	0	0	0	0	0	0	0	0	0
0	0	0	0	0	0	0	1	0	0	0
0	0	0	0	0	0	0	0	0	0	0
0	0	0	0	0	0	0	1	0	0	0
0	0	0	0	0	0	0	0	0	0	0
0	0	0	0	0	0	0	1	0	0	0
0	0	0	0	0	0	0	0	0	0	0
0	0	0	0	0	0	0	1	0	0	0
0	0	0	0	0	0	0	0	0	0	0
0	0	0	0	0	0	0	1	0	0	0
0	0	0	0	0	0	0	0	0	0	0
0	0	0	0	0	0	0	1	0	0	0
0	0	0	0	0	0	0	0	0	0	0
0	0	0	0	0	0	0	1	0	0	0
0	0	0	0	0	0	0	0	0	0	0
0	0	0	0	0	0	0	1	0	0	0
0	0	0	0	0	0	0	0	0	0	0
0	0	0	0	0	0	0	1	0	0	0
0	0	0	0	0	0	0	0	0	0	0
0	0	0	0	0	0	0	1	0	0	0
0	0	0	0	0	0	0	0	0	0	0
0	0	0	0	0	0	0	1	0	0	0
0	0	0	0	0	0	0	0	0	0	0
0	0	0	0	0	0	0	1	0	0	0
0	0	288	0	1	0	0	0	0	0	0
0	0	288	0	1	0	0	1	0	0	0
0	0	549	0	1	0	0	0	0	0	0
0	0	549	0	1	0	0	1	0	0	0
0	0	4608	0	1	0	0	0	0	0	0
0	0	4608	0	1	0	0	1	0	0	0
0	0	2816	0	1	0	0	0	0	0	0
0	0	2816	0	1	0	0	1	0	0	0
0	0	5888	0	1	0	0	0	0	0	0
0	0	5888	0	1	0	0	1	0	0	0
0	0	3847	0	1	0	0	0	0	0	0
0	0	3847	0	1	0	0	1	0	0	0
0	0	4608	0	1	0	0	0	0	0	0
0	0	4608	0	1	0	0	1	0	0	0
0	0	7424	0	1	0	0	0	0	0	0
0	0	7424	0	1	0	0	1	0	0	0
0	0	3338	0	1	0	0	0	0	0	0
0	0	3338	0	1	0	0	1	0	0	0
0	0	5376	0	1	0	0	0	0	0	0
0	0	5376	0	1	0	0	1	0	0	0
0	0	2817	0	1	0	0	0	0	0	0
0	0	2817	0	1	0	0	1	0	0	0
0	0	4608	0	1	0	0	0	0	0	0
0	0	4608	0	1	0	0	1	0	0	0
0	0	2818	0	1	0	0	0	0	0	0
0	0	2818	0	1	0	0	1	0	0	0
0	0	1024	0	1	0	0	0	0	0	0
0	0	1024	0	1	0	0	1	0	0	0
0	0	511	0	1	0	0	0	0	0	0
0	0	511	0	1	0	0	1	0	0	0
0	0	6912	0	1	0	0	0	0	0	0
0	0	6912	0	1	0	0	1	0	0	0
0	0	7424	0	1	0	0	0	0	0	0
0	0	7424	0	1	0	0	1	0	0	0
0	0	3347	0	1	0	0	0	0	0	0
0	0	3347	0	1	0	0	1	0	0	0
0	0	6400	0	1	0	0	0	0	0	0
0	0	6400	0	1	0	0	1	0	0	0
0	0	2819	0	1	0	0	0	0	0	0
0	0	2819	0	1	0	0	1	0	0	0
0	0	2309	0	1	0	0	0	0	0	0
0	0	2309	0	1	0	0	1	0	0	0
0	0	1024	0	1	0	0	0	0	0	0
0	0	1024	0	1	0	0	1	0	0	0
0	0	2562	0	1	0	0	0	0	0	0
0	0	2562	0	1	0	0	1	0	0	0
0	0	5376	0	1	0	0	0	0	0	0
0	0	5376	0	1	0	0	1	0	0	0
0	0	2820	0	1	0	0	0	0	0	0
0	0	2820	0	1	0	0	1	0	0	0
0	0	7936	0	1	0	0	0	0	0	0
0	0	7936	0	1	0	0	1	0	0	0
0	0	0	0	0	1	0	0	0	0	0
0	0	0	0	0	1	0	1	0	0	0
0	0	0	0	0	0	0	0	x	0	0
0	0	0	0	0	0	0	1	x	0	0
0	0	0	0	0	0	0	0	x	0	0
0	0	0	0	0	0	0	1	x	0	0
0	0	0	0	0	0	0	0	x	0	0
0	0	0	0	0	0	0	1	x	0	0
0	0	0	0	0	0	0	0	x	0	0
0	0	0	0	0	0	0	1	x	0	0
0	0	0	0	0	0	0	0	x	0	0
0	0	0	0	0	0	0	1	x	0	0
0	0	0	0	0	0	0	0	x	0	0
0	0	0	0	0	0	0	1	x	0	0
0	0	0	0	0	0	0	0	x	0	0
0	0	0	0	0	0	0	1	x	0	0
0	0	0	0	0	0	0	0	x	0	0
0	0	0	0	0	0	0	1	x	0	0
0	0	0	0	0	0	0	0	x	0	0
0	0	0	0	0	0	0	1	x	0	0
0	0	0	0	0	0	0	0	x	0	0
0	0	0	0	0	0	0	1	x	0	0
0	0	0	0	0	0	0	0	x	0	0
0	0	0	0	0	0	0	1	x	0	0
0	0	0	0	0	0	0	0	x	0	0
0	0	0	0	0	0	0	1	x	0	0
0	0	0	0	0	0	0	0	x	0	0
0	0	0	0	0	0	0	1	x	0	0
0	0	0	0	0	0	0	0	x	0	0
0	0	0	0	0	0	0	1	x	0	0
0	0	0	0	0	0	0	0	x	0	0
0	0	0	0	0	0	0	1	x	0	0
0	0	0	0	0	0	0	0	x	0	0
0	0	0	0	0	0	0	1	x	0	0
0	0	0	0	0	0	0	0	x	0	0
0	0	0	0	0	0	0	1	x	0	0
0	0	0	0	0	0	0	0	x	0	0
0	0	0	0	0	0	0	1	x	0	0
0	0	0	0	0	0	0	0	x	0	0
0	0	0	0	0	0	0	1	x	0	0
0	0	0	0	0	0	0	0	x	0	0
0	0	0	0	0	0	0	1	x	0	0
0	0	0	0	0	0	0	0	x	0	0
0	0	0	0	0	0	0	1	x	0	0
0	0	0	0	0	0	0	0	x	0	0
0	0	0	0	0	0	0	1	x	0	0
0	0	0	0	0	0	0	0	x	0	0
0	0	0	0	0	0	0	1	x	0	0
0	0	0	0	0	0	0	0	x	0	0
0	0	0	0	0	0	0	1	x	0	0
0	0	0	0	0	0	0	0	x	0	0
0	0	0	0	0	0	0	1	x	0	0
0	0	0	0	0	0	0	0	x	0	0
0	0	0	0	0	0	0	1	x	0	0
0	0	0	0	0	0	0	0	x	0	0
0	0	0	0	0	0	0	1	x	0	0
0	0	0	0	0	0	0	0	x	0	0
0	0	0	0	0	0	0	1	x	0	0
0	0	0	0	0	0	0	0	x	0	0
0	0	0	0	0	0	0	1	x	0	0
0	0	0	0	0	0	0	0	x	0	0
0	0	0	0	0	0	0	1	x	0	0
0	0	0	0	0	0	0	0	x	0	0
0	0	0	0	0	0	0	1	x	0	0
0	0	0	0	0	0	0	0	x	0	0
0	0	0	0	0	0	0	1	x	0	0
0	0	0	0	0	0	0	0	x	0	0
0	0	0	0	0	0	0	1	x	0	0
0	0	0	0	0	0	0	0	x	0	0
0	0	0	0	0	0	0	1	x	0	0
0	0	0	0	0	0	0	0	x	0	0
0	0	0	0	0	0	0	1	x	0	0
0	0	0	0	0	0	0	0	x	0	0
0	0	0	0	0	0	0	1	x	0	0
0	0	0	0	0	0	0	0	x	0	0
0	0	0	0	0	0	0	1	x	0	0
0	0	0	0	0	0	0	0	x	0	0
0	0	0	0	0	0	0	1	x	0	0
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*/

/* Test case 06_P01T2:
M	N	progIN	reset	progLoad	start	result	clk	valid	done	output
0	0	0	0	0	0	0	0	x	x	x
0	0	0	0	0	0	0	1	x	x	x
0	0	0	1	0	0	0	0	x	x	x
0	0	0	1	0	0	0	1	0	0	x
0	0	0	0	0	0	0	0	0	0	x
0	0	0	0	0	0	0	1	0	0	x
0	0	0	0	0	0	0	0	0	0	x
0	0	0	0	0	0	0	1	0	0	x
0	0	0	0	0	0	0	0	0	0	x
0	0	0	0	0	0	0	1	0	0	x
0	0	0	0	0	0	0	0	0	0	x
0	0	0	0	0	0	0	1	0	0	x
0	0	0	0	0	0	0	0	0	0	x
0	0	0	0	0	0	0	1	0	0	x
0	0	0	0	0	0	0	0	0	0	x
0	0	0	0	0	0	0	1	0	0	x
0	0	0	0	0	0	0	0	0	0	x
0	0	0	0	0	0	0	1	0	0	x
0	0	0	0	0	0	0	0	0	0	x
0	0	0	0	0	0	0	1	0	0	x
0	0	0	0	0	0	0	0	0	0	x
0	0	0	0	0	0	0	1	0	0	x
0	0	0	0	0	0	0	0	0	0	x
0	0	0	0	0	0	0	1	0	0	x
0	0	0	0	0	0	0	0	0	0	x
0	0	0	0	0	0	0	1	0	0	x
0	0	0	0	0	0	0	0	0	0	x
0	0	0	0	0	0	0	1	0	0	x
0	0	0	0	0	0	0	0	0	0	x
0	0	0	0	0	0	0	1	0	0	x
0	0	0	0	0	0	0	0	0	0	x
0	0	0	0	0	0	0	1	0	0	x
0	0	0	0	0	0	0	0	0	0	x
0	0	0	0	0	0	0	1	0	0	x
0	0	0	0	0	0	0	0	0	0	x
0	0	0	0	0	0	0	1	0	0	x
0	0	0	0	0	0	0	0	0	0	x
0	0	0	0	0	0	0	1	0	0	x
0	0	0	0	0	0	0	0	0	0	x
0	0	0	0	0	0	0	1	0	0	x
0	0	0	0	0	0	0	0	0	0	x
0	0	0	0	0	0	0	1	0	0	x
0	0	0	0	0	0	0	0	0	0	x
0	0	0	0	0	0	0	1	0	0	x
0	0	271	0	1	0	0	0	0	0	x
0	0	271	0	1	0	0	1	0	0	x
0	0	516	0	1	0	0	0	0	0	x
0	0	516	0	1	0	0	1	0	0	x
0	0	5888	0	1	0	0	0	0	0	x
0	0	5888	0	1	0	0	1	0	0	x
0	0	7424	0	1	0	0	0	0	0	x
0	0	7424	0	1	0	0	1	0	0	x
0	0	3345	0	1	0	0	0	0	0	x
0	0	3345	0	1	0	0	1	0	0	x
0	0	507	0	1	0	0	0	0	0	x
0	0	507	0	1	0	0	1	0	0	x
0	0	7424	0	1	0	0	0	0	0	x
0	0	7424	0	1	0	0	1	0	0	x
0	0	3593	0	1	0	0	0	0	0	x
0	0	3593	0	1	0	0	1	0	0	x
0	0	2817	0	1	0	0	0	0	0	x
0	0	2817	0	1	0	0	1	0	0	x
0	0	768	0	1	0	0	0	0	0	x
0	0	768	0	1	0	0	1	0	0	x
0	0	5888	0	1	0	0	0	0	0	x
0	0	5888	0	1	0	0	1	0	0	x
0	0	7424	0	1	0	0	0	0	0	x
0	0	7424	0	1	0	0	1	0	0	x
0	0	4113	0	1	0	0	0	0	0	x
0	0	4113	0	1	0	0	1	0	0	x
0	0	258	0	1	0	0	0	0	0	x
0	0	258	0	1	0	0	1	0	0	x
0	0	7424	0	1	0	0	0	0	0	x
0	0	7424	0	1	0	0	1	0	0	x
0	0	7424	0	1	0	0	0	0	0	x
0	0	7424	0	1	0	0	1	0	0	x
0	0	3346	0	1	0	0	0	0	0	x
0	0	3346	0	1	0	0	1	0	0	x
0	0	2818	0	1	0	0	0	0	0	x
0	0	2818	0	1	0	0	1	0	0	x
0	0	2819	0	1	0	0	0	0	0	x
0	0	2819	0	1	0	0	1	0	0	x
0	0	7936	0	1	0	0	0	0	0	x
0	0	7936	0	1	0	0	1	0	0	x
0	0	0	0	0	1	0	0	0	0	x
0	0	0	0	0	1	0	1	0	0	x
0	0	0	0	0	0	0	0	x	0	x
0	0	0	0	0	0	0	1	x	0	x
0	0	0	0	0	0	0	0	x	0	x
0	0	0	0	0	0	0	1	x	0	x
0	0	0	0	0	0	0	0	x	0	x
0	0	0	0	0	0	0	1	x	0	x
0	0	0	0	0	0	0	0	x	0	x
0	0	0	0	0	0	0	1	x	0	x
0	0	0	0	0	0	0	0	x	0	x
0	0	0	0	0	0	0	1	x	0	x
0	0	0	0	0	0	0	0	x	0	x
0	0	0	0	0	0	0	1	x	0	x
0	0	0	0	0	0	0	0	x	0	x
0	0	0	0	0	0	0	1	x	0	x
0	0	0	0	0	0	0	0	x	0	x
0	0	0	0	0	0	0	1	x	0	x
0	0	0	0	0	0	0	0	x	0	x
0	0	0	0	0	0	0	1	x	0	x
0	0	0	0	0	0	0	0	x	0	x
0	0	0	0	0	0	0	1	x	0	x
0	0	0	0	0	0	0	0	x	0	x
0	0	0	0	0	0	0	1	x	0	x
0	0	0	0	0	0	0	0	x	0	x
0	0	0	0	0	0	0	1	x	0	x
0	0	0	0	0	0	0	0	x	0	x
0	0	0	0	0	0	0	1	x	0	x
0	0	0	0	0	0	0	0	x	0	x
0	0	0	0	0	0	0	1	x	0	x
0	0	0	0	0	0	0	0	x	0	x
0	0	0	0	0	0	0	1	x	0	x
0	0	0	0	0	0	0	0	x	0	x
0	0	0	0	0	0	0	1	x	0	x
0	0	0	0	0	0	0	0	x	0	x
0	0	0	0	0	0	0	1	x	0	x
0	0	0	0	0	0	0	0	x	0	x
0	0	0	0	0	0	0	1	x	0	x
0	0	0	0	0	0	0	0	x	0	x
0	0	0	0	0	0	0	1	x	0	x
0	0	0	0	0	0	0	0	x	0	x
0	0	0	0	0	0	0	1	x	0	x
0	0	0	0	0	0	0	0	x	0	x
0	0	0	0	0	0	0	1	x	0	x
0	0	0	0	0	0	0	0	x	0	x
0	0	0	0	0	0	0	1	x	0	x
0	0	0	0	0	0	0	0	x	0	x
0	0	0	0	0	0	0	1	x	0	x
0	0	0	0	0	0	0	0	x	0	x
0	0	0	0	0	0	0	1	x	0	x
0	0	0	0	0	0	0	0	x	0	x
0	0	0	0	0	0	0	1	x	0	x
0	0	0	0	0	0	0	0	x	0	x
0	0	0	0	0	0	0	1	x	0	x
0	0	0	0	0	0	0	0	x	0	x
0	0	0	0	0	0	0	1	x	0	x
0	0	0	0	0	0	0	0	x	0	x
0	0	0	0	0	0	0	1	x	0	x
0	0	0	0	0	0	0	0	x	0	x
0	0	0	0	0	0	0	1	x	0	x
0	0	0	0	0	0	0	0	x	0	x
0	0	0	0	0	0	0	1	x	0	x
0	0	0	0	0	0	0	0	x	0	x
0	0	0	0	0	0	0	1	x	0	x
0	0	0	0	0	0	0	0	x	0	x
0	0	0	0	0	0	0	1	x	0	x
0	0	0	0	0	0	0	0	x	0	x
0	0	0	0	0	0	0	1	x	0	x
0	0	0	0	0	0	0	0	x	0	x
0	0	0	0	0	0	0	1	x	0	x
0	0	0	0	0	0	0	0	x	0	x
0	0	0	0	0	0	0	1	x	0	x
0	0	0	0	0	0	0	0	x	0	x
0	0	0	0	0	0	0	1	x	0	x
0	0	0	0	0	0	0	0	x	0	x
0	0	0	0	0	0	0	1	x	0	x
0	0	0	0	0	0	0	0	x	0	x
0	0	0	0	0	0	0	1	x	0	x
0	0	0	0	0	0	0	0	x	0	x
0	0	0	0	0	0	0	1	x	0	x
0	0	0	0	0	0	0	0	x	0	x
0	0	0	0	0	0	0	1	x	0	x
0	0	0	0	0	0	0	0	x	0	x
0	0	0	0	0	0	0	1	x	0	x
0	0	0	0	0	0	0	0	x	0	x
0	0	0	0	0	0	0	1	x	0	x
0	0	0	0	0	0	0	0	x	0	x
0	0	0	0	0	0	0	1	x	0	x
0	0	0	0	0	0	0	0	x	0	x
0	0	0	0	0	0	0	1	x	0	x
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*/

/* Test case 02_P01T2:
M	N	progIN	reset	progLoad	start	result	clk	valid	done	output
0	0	0	0	0	0	0	0	x	x	x
0	0	0	0	0	0	0	1	x	x	x
0	0	0	1	0	0	0	0	x	x	x
0	0	0	1	0	0	0	1	0	0	0
0	0	0	0	0	0	0	0	0	0	0
0	0	0	0	0	0	0	1	0	0	0
0	0	0	0	0	0	0	0	0	0	0
0	0	0	0	0	0	0	1	0	0	0
0	0	0	0	0	0	0	0	0	0	0
0	0	0	0	0	0	0	1	0	0	0
0	0	0	0	0	0	0	0	0	0	0
0	0	0	0	0	0	0	1	0	0	0
0	0	0	0	0	0	0	0	0	0	0
0	0	0	0	0	0	0	1	0	0	0
0	0	0	0	0	0	0	0	0	0	0
0	0	0	0	0	0	0	1	0	0	0
0	0	0	0	0	0	0	0	0	0	0
0	0	0	0	0	0	0	1	0	0	0
0	0	0	0	0	0	0	0	0	0	0
0	0	0	0	0	0	0	1	0	0	0
0	0	0	0	0	0	0	0	0	0	0
0	0	0	0	0	0	0	1	0	0	0
0	0	0	0	0	0	0	0	0	0	0
0	0	0	0	0	0	0	1	0	0	0
0	0	0	0	0	0	0	0	0	0	0
0	0	0	0	0	0	0	1	0	0	0
0	0	0	0	0	0	0	0	0	0	0
0	0	0	0	0	0	0	1	0	0	0
0	0	0	0	0	0	0	0	0	0	0
0	0	0	0	0	0	0	1	0	0	0
0	0	0	0	0	0	0	0	0	0	0
0	0	0	0	0	0	0	1	0	0	0
0	0	0	0	0	0	0	0	0	0	0
0	0	0	0	0	0	0	1	0	0	0
0	0	0	0	0	0	0	0	0	0	0
0	0	0	0	0	0	0	1	0	0	0
0	0	0	0	0	0	0	0	0	0	0
0	0	0	0	0	0	0	1	0	0	0
0	0	0	0	0	0	0	0	0	0	0
0	0	0	0	0	0	0	1	0	0	0
0	0	0	0	0	0	0	0	0	0	0
0	0	0	0	0	0	0	1	0	0	0
0	0	271	0	1	0	0	0	0	0	0
0	0	271	0	1	0	0	1	0	0	0
0	0	565	0	1	0	0	0	0	0	0
0	0	565	0	1	0	0	1	0	0	0
0	0	4352	0	1	0	0	0	0	0	0
0	0	4352	0	1	0	0	1	0	0	0
0	0	2819	0	1	0	0	0	0	0	0
0	0	2819	0	1	0	0	1	0	0	0
0	0	7936	0	1	0	0	0	0	0	0
0	0	7936	0	1	0	0	1	0	0	0
0	0	0	0	0	1	0	0	0	0	0
0	0	0	0	0	1	0	1	0	0	0
0	0	0	0	0	0	0	0	x	0	0
0	0	0	0	0	0	0	1	x	0	0
0	0	0	0	0	0	0	0	x	0	0
0	0	0	0	0	0	0	1	x	0	0
0	0	0	0	0	0	0	0	x	0	0
0	0	0	0	0	0	0	1	x	0	0
0	0	0	0	0	0	0	0	x	0	0
0	0	0	0	0	0	0	1	x	0	0
0	0	0	0	0	0	0	0	x	0	0
0	0	0	0	0	0	0	1	x	0	0
0	0	0	0	0	0	0	0	x	0	0
0	0	0	0	0	0	0	1	x	0	0
0	0	0	0	0	0	0	0	x	0	0
0	0	0	0	0	0	0	1	x	0	0
0	0	0	0	0	0	0	0	x	0	0
0	0	0	0	0	0	0	1	x	0	0
0	0	0	0	0	0	0	0	x	0	0
0	0	0	0	0	0	0	1	x	0	0
0	0	0	0	0	0	0	0	x	0	0
0	0	0	0	0	0	0	1	x	0	0
0	0	0	0	0	0	0	0	x	0	0
0	0	0	0	0	0	0	1	x	0	0
0	0	0	0	0	0	0	0	x	0	0
0	0	0	0	0	0	0	1	x	0	0
0	0	0	0	0	0	0	0	x	0	0
0	0	0	0	0	0	0	1	x	0	0
0	0	0	0	0	0	0	0	x	0	0
0	0	0	0	0	0	0	1	x	0	0
0	0	0	0	0	0	0	0	x	0	0
0	0	0	0	0	0	0	1	x	0	0
0	0	0	0	0	0	0	0	x	0	0
0	0	0	0	0	0	0	1	x	0	0
0	0	0	0	0	0	0	0	x	0	0
0	0	0	0	0	0	0	1	x	0	0
0	0	0	0	0	0	0	0	x	0	0
0	0	0	0	0	0	0	1	x	0	0
0	0	0	0	0	0	0	0	x	0	0
0	0	0	0	0	0	0	1	x	0	0
0	0	0	0	0	0	0	0	x	0	0
0	0	0	0	0	0	0	1	x	0	0
0	0	0	0	0	0	0	0	x	0	0
0	0	0	0	0	0	0	1	x	0	0
0	0	0	0	0	0	0	0	x	0	0
0	0	0	0	0	0	0	1	x	0	0
0	0	0	0	0	0	0	0	x	0	0
0	0	0	0	0	0	0	1	x	0	0
0	0	0	0	0	0	0	0	x	0	0
0	0	0	0	0	0	0	1	x	0	0
0	0	0	0	0	0	0	0	x	0	0
0	0	0	0	0	0	0	1	x	0	0
0	0	0	0	0	0	0	0	x	0	0
0	0	0	0	0	0	0	1	1	0	0
0	0	0	0	0	0	1	0	1	0	0
0	0	0	0	0	0	1	1	1	0	0
0	0	0	0	0	0	0	0	1	0	0
0	0	0	0	0	0	0	1	1	0	0
0	0	0	0	0	0	0	0	1	0	0
0	0	0	0	0	0	0	1	1	0	0
0	0	0	0	0	0	0	0	1	0	0
0	0	0	0	0	0	0	1	1	0	68
0	0	0	0	0	0	0	0	1	0	68
0	0	0	0	0	0	0	1	1	0	0
0	0	0	0	0	0	0	0	1	0	0
0	0	0	0	0	0	0	1	1	0	0
0	0	0	0	0	0	0	0	1	0	0
0	0	0	0	0	0	0	1	1	0	0
0	0	0	0	0	0	0	0	1	0	0
0	0	0	0	0	0	0	1	1	0	0
0	0	0	0	0	0	0	0	1	0	0
0	0	0	0	0	0	0	1	1	0	0
0	0	0	0	0	0	0	0	1	0	0
0	0	0	0	0	0	0	1	1	0	0
0	0	0	0	0	0	0	0	1	0	0
0	0	0	0	0	0	0	1	1	0	0
0	0	0	0	0	0	0	0	1	0	0
0	0	0	0	0	0	0	1	1	0	0
0	0	0	0	0	0	0	0	1	0	0
0	0	0	0	0	0	0	1	1	0	0
0	0	0	0	0	0	0	0	1	0	0
0	0	0	0	0	0	0	1	1	0	0
0	0	0	0	0	0	0	0	1	0	0
0	0	0	0	0	0	0	1	1	0	0
0	0	0	0	0	0	0	0	1	0	0
0	0	0	0	0	0	0	1	1	0	0
0	0	0	0	0	0	0	0	1	0	0
0	0	0	0	0	0	0	1	1	1	0
0	0	0	0	0	0	0	0	1	1	0
0	0	0	0	0	0	0	1	1	1	0
0	0	0	0	0	0	0	0	1	1	0
0	0	0	0	0	0	0	1	1	1	0
0	0	0	0	0	0	1	0	1	X	0
0	0	0	0	0	0	1	1	1	X	0
0	0	0	0	0	0	0	0	1	0	0
0	0	0	0	0	0	0	1	1	0	0
0	0	0	0	0	0	0	0	1	0	0
0	0	0	0	0	0	0	1	1	0	0
0	0	0	0	0	0	0	0	1	0	0
0	0	0	0	0	0	0	1	1	0	68
0	0	0	0	0	0	0	0	1	0	68
0	0	0	0	0	0	0	1	1	0	0
0	0	0	0	0	0	0	0	1	0	0
0	0	0	0	0	0	0	1	1	0	0
0	0	0	0	0	0	0	0	1	0	0
0	0	0	0	0	0	0	1	1	0	0
0	0	0	0	0	0	0	0	1	0	0
0	0	0	0	0	0	0	1	1	0	0
0	0	0	0	0	0	0	0	1	0	0
0	0	0	0	0	0	0	1	1	0	0
0	0	0	0	0	0	0	0	1	0	0
0	0	0	0	0	0	0	1	1	0	0
0	0	0	0	0	0	0	0	1	0	0
0	0	0	0	0	0	0	1	1	0	0
0	0	0	0	0	0	0	0	1	0	0
0	0	0	0	0	0	0	1	1	0	0
0	0	0	0	0	0	0	0	1	0	0
0	0	0	0	0	0	0	1	1	0	0
0	0	0	0	0	0	0	0	1	0	0
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*/

/* Test case Test all:
M	N	progIN	reset	progLoad	start	result	clk	valid	done	output
2	15	0	0	0	0	0	0	x	x	x
2	15	0	0	0	0	0	1	x	x	x
2	15	0	1	0	0	0	0	0	0	0
2	15	0	1	0	0	0	1	0	0	0
2	15	0	0	0	0	0	0	0	0	0
2	15	0	0	0	0	0	1	0	0	0
2	15	0	0	0	0	0	0	0	0	0
2	15	0	0	0	0	0	1	0	0	0
2	15	0	0	0	0	0	0	0	0	0
2	15	0	0	0	0	0	1	0	0	0
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*/

/* Test case triple:
M	N	progIN	reset	progLoad	start	result	clk	valid	done	output
0	0	0	0	0	0	0	0	x	x	x
0	0	0	0	0	0	0	1	x	x	x
0	0	0	1	0	0	0	0	x	x	x
0	0	0	1	0	0	0	1	0	0	0
0	0	0	0	0	0	0	0	0	0	0
0	0	0	0	0	0	0	1	0	0	0
0	0	0	0	0	0	0	0	0	0	0
0	0	0	0	0	0	0	1	0	0	0
0	0	0	0	0	0	0	0	0	0	0
0	0	0	0	0	0	0	1	0	0	0
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*/

/* Test case 1.5 : 1:
M	N	progIN	reset	progLoad	start	result	clk	valid	done	output
0	0	0	0	0	0	0	0	x	x	x
0	0	0	0	0	0	0	1	x	x	x
0	0	0	1	0	0	0	0	0	0	0
0	0	0	1	0	0	0	1	0	0	0
0	0	0	0	0	0	0	0	0	0	0
0	0	0	0	0	0	0	1	0	0	0
0	0	0	0	0	0	0	0	0	0	0
0	0	0	0	0	0	0	1	0	0	0
0	0	0	0	0	0	0	0	0	0	0
0	0	0	0	0	0	0	1	0	0	0
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*/

/* Test case playwithresetMN:
M	N	progIN	reset	progLoad	start	result	clk	valid	done	output
0	0	0	0	0	0	0	0	x	x	x
0	0	0	0	0	0	0	1	x	x	x
0	0	0	1	0	0	0	0	0	0	0
0	0	0	1	0	0	0	1	0	0	0
0	0	0	0	0	0	0	0	0	0	0
0	0	0	0	0	0	0	1	0	0	0
0	0	0	0	0	0	0	0	0	0	0
0	0	0	0	0	0	0	1	0	0	0
0	0	0	0	0	0	0	0	0	0	0
0	0	0	0	0	0	0	1	0	0	0
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*/

/* Test case 07_P01T3:
M	N	progIN	reset	progLoad	start	result	clk	valid	done	output
0	0	0	0	0	0	0	0	x	x	x
0	0	0	0	0	0	0	1	x	x	x
0	0	0	1	0	0	0	0	x	x	x
0	0	0	1	0	0	0	1	0	0	x
0	0	0	0	0	0	0	0	0	0	x
0	0	0	0	0	0	0	1	0	0	x
0	0	0	0	0	0	0	0	0	0	x
0	0	0	0	0	0	0	1	0	0	x
0	0	0	0	0	0	0	0	0	0	x
0	0	0	0	0	0	0	1	0	0	x
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*/

/* Test case 03_P01T2:
M	N	progIN	reset	progLoad	start	result	clk	valid	done	output
0	0	0	0	0	0	0	0	x	x	x
0	0	0	0	0	0	0	1	x	x	x
0	0	0	1	0	0	0	0	x	x	x
0	0	0	1	0	0	0	1	0	0	0
0	0	0	0	0	0	0	0	0	0	0
0	0	0	0	0	0	0	1	0	0	0
0	0	0	0	0	0	0	0	0	0	0
0	0	0	0	0	0	0	1	0	0	0
0	0	0	0	0	0	0	0	0	0	0
0	0	0	0	0	0	0	1	0	0	0
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*/

/* Test case Shift test 1:
M	N	progIN	reset	progLoad	start	result	clk	valid	done	output
0	0	0	0	0	0	0	0	x	x	x
0	0	0	0	0	0	0	1	x	x	x
0	0	0	1	0	0	0	0	0	0	0
0	0	0	1	0	0	0	1	0	0	0
0	0	0	0	0	0	0	0	0	0	0
0	0	0	0	0	0	0	1	0	0	0
0	0	0	0	0	0	0	0	0	0	0
0	0	0	0	0	0	0	1	0	0	0
0	0	0	0	0	0	0	0	0	0	0
0	0	0	0	0	0	0	1	0	0	0
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*/

/* Test case Jump:
M	N	progIN	reset	progLoad	start	result	clk	valid	done	output
0	0	0	0	0	0	0	0	x	x	x
0	0	0	0	0	0	0	1	x	x	x
0	0	0	1	0	0	0	0	x	x	x
0	0	0	1	0	0	0	1	0	0	0
0	0	0	0	0	0	0	0	0	0	0
0	0	0	0	0	0	0	1	0	0	0
0	0	0	0	0	0	0	0	0	0	0
0	0	0	0	0	0	0	1	0	0	0
0	0	0	0	0	0	0	0	0	0	0
0	0	0	0	0	0	0	1	0	0	0
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*/

/* Test case Overwritelvl1:
M N progIN reset progLoad start result clk valid done output	
0 0 0 0 0 0 0 0 x x x	
0 0 0 0 0 0 0 1 x x x	
0 0 0 1 0 0 0 0 0 0 0	
0 0 0 1 0 0 0 1 0 0 0	
0 0 0 0 0 0 0 0 0 0 0	
0 0 0 0 0 0 0 1 0 0 0	
0 0 0 0 0 0 0 0 0 0 0	
0 0 0 0 0 0 0 1 0 0 0	
0 0 0 0 0 0 0 0 0 0 0	
0 0 0 0 0 0 0 1 0 0 0	
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*/

/* Test case compy:
M N progIN reset progLoad start result clk valid done output
0 0 0 0 0 0 0 0 x x x
0 0 0 0 0 0 0 1 x x x
0 0 0 1 0 0 0 0 0 0 0
0 0 0 1 0 0 0 1 0 0 0
0 0 0 0 0 0 0 0 0 0 0
0 0 0 0 0 0 0 1 0 0 0
0 0 0 0 0 0 0 0 0 0 0
0 0 0 0 0 0 0 1 0 0 0
0 0 0 0 0 0 0 0 0 0 0
0 0 0 0 0 0 0 1 0 0 0
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*/

/* Test case 08_P01T3:
M	N	progIN	reset	progLoad	start	result	clk	valid	done	output
0	0	0	0	0	0	0	0	x	x	x
0	0	0	0	0	0	0	1	x	x	x
0	0	0	1	0	0	0	0	x	x	x
0	0	0	1	0	0	0	1	0	0	x
0	0	0	0	0	0	0	0	0	0	x
0	0	0	0	0	0	0	1	0	0	x
0	0	0	0	0	0	0	0	0	0	x
0	0	0	0	0	0	0	1	0	0	x
0	0	0	0	0	0	0	0	0	0	x
0	0	0	0	0	0	0	1	0	0	x
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*/

/* Test case 04_P01T2:
M	N	progIN	reset	progLoad	start	result	clk	valid	done	output
0	0	0	0	0	0	0	0	x	x	x
0	0	0	0	0	0	0	1	x	x	x
0	0	0	1	0	0	0	0	x	x	x
0	0	0	1	0	0	0	1	0	0	0
0	0	0	0	0	0	0	0	0	0	0
0	0	0	0	0	0	0	1	0	0	0
0	0	0	0	0	0	0	0	0	0	0
0	0	0	0	0	0	0	1	0	0	0
0	0	0	0	0	0	0	0	0	0	0
0	0	0	0	0	0	0	1	0	0	0
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*/

/* Test case pRamLoad:
M	N	progIN	reset	progLoad	start	result	clk	valid	done	output
0	0	0	0	0	0	0	0	x	x	x
0	0	0	0	0	0	0	1	x	x	x
0	0	0	1	0	0	0	0	x	x	x
0	0	0	1	0	0	0	1	0	0	0
0	0	0	0	0	0	0	0	0	0	0
0	0	0	0	0	0	0	1	0	0	0
0	0	0	0	0	0	0	0	0	0	0
0	0	0	0	0	0	0	1	0	0	0
0	0	0	0	0	0	0	0	0	0	0
0	0	0	0	0	0	0	1	0	0	0
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*/

/* Test case 01_P01T01:
M	N	progIN	reset	progLoad	start	result	clk	valid	done	output
0	0	0	0	0	0	0	0	x	x	x
0	0	0	0	0	0	0	1	x	x	x
0	0	0	1	0	0	0	0	0	0	0
0	0	0	1	0	0	0	1	0	0	0
0	0	0	0	0	0	0	0	0	0	0
0	0	0	0	0	0	0	1	0	0	0
0	0	0	0	0	0	0	0	0	0	0
0	0	0	0	0	0	0	1	0	0	0
0	0	0	0	0	0	0	0	0	0	0
0	0	0	0	0	0	0	1	0	0	0
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*/

/* Test case test11:
M N progIN reset progLoad start result clk valid done output
0 0 0 0 0 0 0 0 x x x
0 0 0 0 0 0 0 1 x x x
0 0 0 1 0 0 0 0 x x x
0 0 0 1 0 0 0 1 0 0 x
0 0 0 0 0 0 0 0 0 0 x
0 0 0 0 0 0 0 1 0 0 x
0 0 0 0 0 0 0 0 0 0 x
0 0 0 0 0 0 0 1 0 0 x
0 0 0 0 0 0 0 0 0 0 x
0 0 0 0 0 0 0 1 0 0 x
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*/

/* Test case How did I get here:
M N progIN reset progLoad start result clk valid done output
0 0 0 0 0 0 0 0 x x x
0 0 0 0 0 0 0 1 x x x
0 0 0 1 0 0 0 0 0 0 0
0 0 0 1 0 0 0 1 0 0 0
0 0 0 0 0 0 0 0 0 0 0
0 0 0 0 0 0 0 1 0 0 0
0 0 0 0 0 0 0 0 0 0 0
0 0 0 0 0 0 0 1 0 0 0
0 0 0 0 0 0 0 0 0 0 0
0 0 0 0 0 0 0 1 0 0 0
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*/

/* Test case Overwrite god:
M	N	progIN	reset	progLoad	start	result	clk	valid	done	output
0	0	0	0	0	0	0	0	x	x	x
0	0	0	0	0	0	0	1	x	x	x
0	0	0	1	0	0	0	0	0	0	0
0	0	0	1	0	0	0	1	0	0	0
0	0	0	0	0	0	0	0	0	0	0
0	0	0	0	0	0	0	1	0	0	0
0	0	0	0	0	0	0	0	0	0	0
0	0	0	0	0	0	0	1	0	0	0
0	0	0	0	0	0	0	0	0	0	0
0	0	0	0	0	0	0	1	0	0	0
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*/

/* Test case 05_P01T2:
M	N	progIN	reset	progLoad	start	result	clk	valid	done	output
0	0	0	0	0	0	0	0	x	x	x
0	0	0	0	0	0	0	1	x	x	x
0	0	0	1	0	0	0	0	x	x	x
0	0	0	1	0	0	0	1	0	0	0
0	0	0	0	0	0	0	0	0	0	0
0	0	0	0	0	0	0	1	0	0	0
0	0	0	0	0	0	0	0	0	0	0
0	0	0	0	0	0	0	1	0	0	0
0	0	0	0	0	0	0	0	0	0	0
0	0	0	0	0	0	0	1	0	0	0
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*/

/* Test case comment19:
M	N	progIN	reset	progLoad	start	result	clk	valid	done	output
0	0	0	0	0	0	0	0	0	0	0
0	0	0	0	0	0	0	1	0	0	0
0	0	0	1	0	0	0	0	0	0	0
0	0	0	1	0	0	0	1	0	0	0
0	0	0	0	0	0	0	0	0	0	0
0	0	0	0	0	0	0	1	0	0	0
0	0	0	0	0	0	0	0	0	0	0
0	0	0	0	0	0	0	1	0	0	0
0	0	0	0	0	0	0	0	0	0	0
0	0	0	0	0	0	0	1	0	0	0
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*/

/* Test case Prime:
M	N	progIN	reset	progLoad	start	result	clk	valid	done	output
0	0	0	0	0	0	0	0	x	x	x
0	0	0	0	0	0	0	1	x	x	x
0	0	0	1	0	0	0	0	x	x	x
0	0	0	1	0	0	0	1	0	0	0
0	0	0	0	0	0	0	0	0	0	0
0	0	0	0	0	0	0	1	0	0	0
0	0	0	0	0	0	0	0	0	0	0
0	0	0	0	0	0	0	1	0	0	0
0	0	0	0	0	0	0	0	0	0	0
0	0	0	0	0	0	0	1	0	0	0
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*/

/* Test case 09:
M N progIN reset progLoad start result clk valid done output
0 0 0 0 0 0 0 0 x x x
0 0 0 0 0 0 0 1 x x x
0 0 0 1 0 0 0 0 x x x
0 0 0 1 0 0 0 1 0 0 x
0 0 0 0 0 0 0 0 0 0 x
0 0 0 0 0 0 0 1 0 0 x
0 0 0 0 0 0 0 0 0 0 x
0 0 0 0 0 0 0 1 0 0 x
0 0 0 0 0 0 0 0 0 0 x
0 0 0 0 0 0 0 1 0 0 x
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*/

/* Test case 11:
M N progIN reset progLoad start result clk valid done output
0 0 0 0 0 0 0 0 x x x
0 0 0 0 0 0 0 1 x x x
0 0 0 1 0 0 0 0 x x x
0 0 0 1 0 0 0 1 0 0 x
0 0 0 0 0 0 0 0 0 0 x
0 0 0 0 0 0 0 1 0 0 x
0 0 0 0 0 0 0 0 0 0 x
0 0 0 0 0 0 0 1 0 0 x
0 0 0 0 0 0 0 0 0 0 x
0 0 0 0 0 0 0 1 0 0 x
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*/

/* Test case 13:
M N progIN reset progLoad start result clk valid done output
0 0 0 0 0 0 0 0 x x x
0 0 0 0 0 0 0 1 x x x
0 0 0 1 0 0 0 0 x x x
0 0 0 1 0 0 0 1 0 0 x
0 0 0 0 0 0 0 0 0 0 x
0 0 0 0 0 0 0 1 0 0 x
0 0 0 0 0 0 0 0 0 0 x
0 0 0 0 0 0 0 1 0 0 x
0 0 0 0 0 0 0 0 0 0 x
0 0 0 0 0 0 0 1 0 0 x
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*/

/* Test case 10:
M N progIN reset progLoad start result clk valid done output
0 0 0 0 0 0 0 0 x x x
0 0 0 0 0 0 0 1 x x x
0 0 0 1 0 0 0 0 x x x
0 0 0 1 0 0 0 1 0 0 x
0 0 0 0 0 0 0 0 0 0 x
0 0 0 0 0 0 0 1 0 0 x
0 0 0 0 0 0 0 0 0 0 x
0 0 0 0 0 0 0 1 0 0 x
0 0 0 0 0 0 0 0 0 0 x
0 0 0 0 0 0 0 1 0 0 x
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*/

/* Test case 12:
M N progIN reset progLoad start result clk valid done output
0 0 0 0 0 0 0 0 x x x
0 0 0 0 0 0 0 1 x x x
0 0 0 1 0 0 0 0 x x x
0 0 0 1 0 0 0 1 0 0 x
0 0 0 0 0 0 0 0 0 0 x
0 0 0 0 0 0 0 1 0 0 x
0 0 0 0 0 0 0 0 0 0 x
0 0 0 0 0 0 0 1 0 0 x
0 0 0 0 0 0 0 0 0 0 x
0 0 0 0 0 0 0 1 0 0 x
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*/

/* Test case 14:
M N progIN reset progLoad start result clk valid done output
0 0 0 0 0 0 0 0 x x x
0 0 0 0 0 0 0 1 x x x
0 0 0 1 0 0 0 0 x x x
0 0 0 1 0 0 0 1 0 0 x
0 0 0 0 0 0 0 0 0 0 x
0 0 0 0 0 0 0 1 0 0 x
0 0 0 0 0 0 0 0 0 0 x
0 0 0 0 0 0 0 1 0 0 x
0 0 0 0 0 0 0 0 0 0 x
0 0 0 0 0 0 0 1 0 0 x
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*/
